# Fritzing sketch Esquematico (saved by Fritzing 0.9.3b)
circuit board: 4.73619cm x 4.79348cm
breadboards: 1

parts:
  U1 = ESP8266 WiFi Module [part_number=ESP8266]
  BMP280_Breakout1 = BMP280 Breakout Board [part_number=BMP280]
  Componente1 = Arduino Uno (Rev3)
  DHT1 = DHT11 Humitidy and Temperature Sensor

nets:
  VCC: U1.VCC, BMP280_Breakout1.VCC, BMP280_Breakout1.SDO, Componente1.3V3
  N1: U1.GPIO_0, BMP280_Breakout1.SDA
  N2: U1.GPIO_2, BMP280_Breakout1.SCL
  GND: U1.GND, BMP280_Breakout1.GND, Componente1.GND, DHT1.GND
  N3: U1.TXD, DHT1.DATA
  5V: Componente1.5V, DHT1.VDD

custom parts:
  ESP8266 WiFi Module: Generic WiFi Module based on the ESP8266 with onboard PCB antenna and UART communications
  BMP280 Breakout Board: This is a breakout board for the Bosch Sensortec BMP280, "an absolute barometric pressure sensor especially designed for mobile applications." The operation range is 300 to 1100 hPa. Supply voltage is 1.2 to 3.6V. Operating temperature range is -40 to +85 °C.
  DHT11 Humitidy and Temperature Sensor: DHT11 Humidity and Temperature Sensor
